# Fritzing sketch SensorHub (saved by Fritzing 0.9.3b)
breadboards: 1

parts:
  Raspberry_Pi_1 = Raspberry Pi 3 [part_number=RPI-3-V1.2]
  R1 = Resistor [tolerance=±5% resistance=10k package=THT]
  R2 = Resistor [tolerance=±5% resistance=10k package=THT]
  R3 = Photocell (LDR) [package=THT]
  Part1 = MQ-7 breakout
  IC1 = MCP3008 8-channel 10-bit ADC [part_number=MCP3008]
  DHT1 = DHT11 Humitidy and Temperature Sensor

nets (from the schematic view):
  3V3: Raspberry_Pi_1.3v3, Raspberry_Pi_1.3V3, R1.Pin_0, Part1.VCC, IC1.no_name_yet#15, IC1.no_name_yet#16
  GND: Raspberry_Pi_1.GND, R3.pin_1, Part1.GND, IC1.no_name_yet#9, IC1.no_name_yet#14, DHT1.GND
  N1: Raspberry_Pi_1.GIPO10, IC1.no_name_yet#11
  N2: Raspberry_Pi_1.GIPO9, IC1.no_name_yet#12
  N3: Raspberry_Pi_1.GIPO11, IC1.no_name_yet#13
  N4: Raspberry_Pi_1.GIPO5, DHT1.DATA
  N5: Raspberry_Pi_1.GIPO8, IC1.no_name_yet#10
  5V: Raspberry_Pi_1.5V, DHT1.VDD
  N6: R1.Pin_1, R2.Pin_0
  N7: R2.Pin_1, R3.pin_0, IC1.no_name_yet#1
  N8: Part1.AO, IC1.no_name_yet#7

custom parts:
  MQ-7 breakout: SKU: 101282
  DHT11 Humitidy and Temperature Sensor: DHT11 Humidity and Temperature Sensor
